# Fritzing sketch Lab 1 Layout (saved by Fritzing 0.9.4)
breadboards: 2

parts:
  U1 = 7400 4 x 2 Input NAND Gate [part_number=7400 package="DIP (Dual Inline) [THT]"]  # not connected
  U2 = 7400 4 x 2 Input NAND Gate [part_number=7400 package="DIP (Dual Inline) [THT]"]  # not connected
  LED1 = smd LED [color="Red (633nm)" package="0805 [SMD]"]
  LED2 = smd LED [color="Red (633nm)" package="0805 [SMD]"]
  LED3 = smd LED [color="Red (633nm)" package="0805 [SMD]"]
  S1 = SWITCH-MOMENTARY-2 [package=reed_switch_pth]
  S2 = SWITCH-MOMENTARY-2 [package=reed_switch_pth]
  S3 = SWITCH-MOMENTARY-2 [package=reed_switch_pth]
  LED4 = smd LED [color="Red (633nm)" package="0805 [SMD]"]  # not connected
  C1 = Tantalum Capacitor [capacitance=1μF package="200 mil [THT, tantalum]"]

nets:
  N1: LED1.cathode, LED2.cathode, LED3.cathode, S1.2, S2.2, S3.2, C1.+
